// Logisim project clock.circ as structural Verilog: 8 circuits, main circuit main
module main (
  output out_1,
  output [3:0] out_2,
  output [3:0] out_3,
  output [3:0] out_4,
  output [3:0] out_5,
  output [3:0] out_6,
  output [3:0] out_7
);

  wire atom_unit_5_1_overflow, atom_unit_5_2_overflow, atom_unit_9_1_overflow, atom_unit_9_hour_1_overflow,
       atom_unit_9_minute_1_overflow, clock_1_out;
  wire [3:0] atom_unit_2_1_out, atom_unit_5_1_out, atom_unit_5_2_out, atom_unit_9_1_out,
       atom_unit_9_hour_1_out, atom_unit_9_minute_1_out;

  Clock clock_1 (.out(clock_1_out));
  atom_unit_2 atom_unit_2_1 (
    .in(out_2), .overflow(out_1), .out(atom_unit_2_1_out), .in_overflow(atom_unit_9_hour_1_overflow));
  atom_unit_9_hour atom_unit_9_hour_1 (
    ._2nd(out_2), .in(out_3), .overflow(atom_unit_9_hour_1_overflow), .out(atom_unit_9_hour_1_out),
    .in_overflow(atom_unit_5_1_overflow));
  molecule_flipflop_d molecule_flipflop_d_1 (.d(atom_unit_2_1_out), .q(out_2), .clk(clock_1_out));
  Hex_Digit_Display hex_digit_display_1 (.value(out_2));  // open: dp
  molecule_flipflop_d molecule_flipflop_d_2 (.d(atom_unit_9_hour_1_out), .q(out_3), .clk(clock_1_out));
  Hex_Digit_Display hex_digit_display_2 (.value(out_3));  // open: dp
  atom_unit_5 atom_unit_5_1 (
    .in(out_4), .overflow(atom_unit_5_1_overflow), .out(atom_unit_5_1_out),
    .in_overflow(atom_unit_9_minute_1_overflow));
  molecule_flipflop_d molecule_flipflop_d_3 (.d(atom_unit_5_1_out), .q(out_4), .clk(clock_1_out));
  Hex_Digit_Display hex_digit_display_3 (.value(out_4));  // open: dp
  atom_unit_9_minute atom_unit_9_minute_1 (
    .in(out_5), .overflow(atom_unit_9_minute_1_overflow), .out(atom_unit_9_minute_1_out),
    .in_overflow(atom_unit_5_2_overflow));
  molecule_flipflop_d molecule_flipflop_d_4 (.d(atom_unit_9_minute_1_out), .q(out_5), .clk(clock_1_out));
  Hex_Digit_Display hex_digit_display_4 (.value(out_5));  // open: dp
  Hex_Digit_Display hex_digit_display_5 (.value(out_6));  // open: dp
  atom_unit_5 atom_unit_5_2 (
    .in(out_6), .overflow(atom_unit_5_2_overflow), .out(atom_unit_5_2_out),
    .in_overflow(atom_unit_9_1_overflow));
  Hex_Digit_Display hex_digit_display_6 (.value(out_7));  // open: dp
  atom_unit_9 atom_unit_9_1 (.in(out_7), .overflow(atom_unit_9_1_overflow), .out(atom_unit_9_1_out));
  molecule_flipflop_d molecule_flipflop_d_5 (.d(atom_unit_5_2_out), .q(out_6), .clk(clock_1_out));
  molecule_flipflop_d molecule_flipflop_d_6 (.d(atom_unit_9_1_out), .q(out_7), .clk(clock_1_out));
endmodule

module molecule_flipflop_d (
  input  [3:0] d,
  input  clk,
  output [3:0] q
);

  atom_flipflop_d atom_flipflop_d_1 (.clk(clk), .d(d[0]), .q(q[0]));
  atom_flipflop_d atom_flipflop_d_2 (.clk(clk), .d(d[1]), .q(q[1]));
  atom_flipflop_d atom_flipflop_d_3 (.clk(clk), .d(d[2]), .q(q[2]));
  atom_flipflop_d atom_flipflop_d_4 (.clk(clk), .d(d[3]), .q(q[3]));
endmodule

module atom_flipflop_d (
  input  clk,
  input  d,
  output q
);

  wire nand_1_out, nand_2_out, nand_3_out, nand_4_out, nand_6_out;

  nand nand_1 (nand_1_out, nand_4_out, nand_2_out);
  nand nand_2 (nand_2_out, nand_1_out, clk);
  nand nand_3 (nand_3_out, nand_2_out, clk, nand_4_out);
  nand nand_4 (nand_4_out, nand_3_out, d);
  nand nand_5 (q, nand_2_out, nand_6_out);
  nand nand_6 (nand_6_out, q, nand_3_out);
endmodule

module atom_unit_9 (
  input  [3:0] in,
  output overflow,
  output [3:0] out
);

  wire [3:0] adder_1_out;

  Adder #(.width(4)) adder_1 (.a(in), .b(4'b0001), .out(adder_1_out));  // open: cin, cout
  and and_1 (overflow, in[0], ~in[1], ~in[2], in[3]);  // AND_Gate
  Multiplexer #(.width(4)) multiplexer_1 (.in0(adder_1_out), .in1(4'b0000), .out(out), .sel(overflow));  // open: en
endmodule

module atom_unit_9_minute (
  input  in_overflow,
  input  [3:0] in,
  output overflow,
  output [3:0] out
);

  wire and_1_out, and_2_out;
  wire [3:0] adder_1_out, multiplexer_1_out;

  Adder #(.width(4)) adder_1 (.a(in), .b(4'b0001), .out(adder_1_out));  // open: cin, cout
  Multiplexer #(.width(4)) multiplexer_1 (
    .in0(in), .in1(adder_1_out), .out(multiplexer_1_out), .sel(in_overflow));  // open: en
  and and_1 (and_1_out, in[0], ~in[1], ~in[2], in[3]);  // AND_Gate
  and and_2 (and_2_out, in_overflow, and_1_out);
  Multiplexer #(.width(4)) multiplexer_2 (
    .in0(multiplexer_1_out), .in1(4'b0000), .out(out), .sel(and_2_out));  // open: en
  and and_3 (overflow, and_1_out, in_overflow);
endmodule

module atom_unit_5 (
  input  in_overflow,
  input  [3:0] in,
  output overflow,
  output [3:0] out
);

  wire and_1_out, and_2_out;
  wire [3:0] adder_1_out, multiplexer_1_out;

  Adder #(.width(4)) adder_1 (.a(in), .b(4'b0001), .out(adder_1_out));  // open: cin, cout
  Multiplexer #(.width(4)) multiplexer_1 (
    .in0(in), .in1(adder_1_out), .out(multiplexer_1_out), .sel(in_overflow));  // open: en
  and and_1 (and_1_out, in[0], ~in[1], in[2], ~in[3]);  // AND_Gate
  and and_2 (and_2_out, in_overflow, and_1_out);
  Multiplexer #(.width(4)) multiplexer_2 (
    .in0(multiplexer_1_out), .in1(4'b0000), .out(out), .sel(and_2_out));  // open: en
  and and_3 (overflow, and_1_out, in_overflow);
endmodule

module atom_unit_9_hour (
  input  [3:0] _2nd,
  input  in_overflow,
  input  [3:0] in,
  output overflow,
  output [3:0] out
);

  wire and_1_out, and_2_out, and_3_out, and_5_out, multiplexer_2_out;
  wire [3:0] adder_1_out, multiplexer_1_out;

  Multiplexer #(.width(4)) multiplexer_1 (
    .in0(in), .in1(adder_1_out), .out(multiplexer_1_out), .sel(in_overflow));  // open: en
  Adder #(.width(4)) adder_1 (.a(in), .b(4'b0001), .out(adder_1_out));  // open: cin, cout
  and and_1 (and_1_out, ~_2nd[0], _2nd[1], ~_2nd[2], ~_2nd[3]);  // AND_Gate
  and and_2 (and_2_out, in[0], ~in[1], ~in[2], in[3]);  // AND_Gate
  and and_3 (and_3_out, in[0], in[1], ~in[2], ~in[3]);  // AND_Gate
  Multiplexer multiplexer_2 (.in0(and_2_out), .in1(and_3_out), .out(multiplexer_2_out), .sel(and_1_out));  // open: en
  and and_4 (overflow, multiplexer_2_out, in_overflow);
  and and_5 (and_5_out, in_overflow, multiplexer_2_out);
  Multiplexer #(.width(4)) multiplexer_3 (
    .in0(multiplexer_1_out), .in1(4'b0000), .out(out), .sel(and_5_out));  // open: en
endmodule

module atom_unit_2 (
  input  in_overflow,
  input  [3:0] in,
  output overflow,
  output [3:0] out
);

  wire and_1_out, and_2_out;
  wire [3:0] adder_1_out, multiplexer_1_out;

  Adder #(.width(4)) adder_1 (.a(in), .b(4'b0001), .out(adder_1_out));  // open: cin, cout
  Multiplexer #(.width(4)) multiplexer_1 (
    .in0(in), .in1(adder_1_out), .out(multiplexer_1_out), .sel(in_overflow));  // open: en
  and and_1 (and_1_out, ~in[0], in[1], ~in[2], ~in[3]);  // AND_Gate
  and and_2 (and_2_out, in_overflow, and_1_out);
  Multiplexer #(.width(4)) multiplexer_2 (
    .in0(multiplexer_1_out), .in1(4'b0000), .out(out), .sel(and_2_out));  // open: en
  and and_3 (overflow, and_1_out, in_overflow);
endmodule
