// Logisim project main.circ as structural Verilog: 17 circuits, main circuit main
module main (
  input  CLR,
  output OVERFLOW,
  output ZERO,
  output [4:0] OpCode
);

  wire CLK_out, microprocessor_1_store, not_1_out;
  wire [4:0] microprocessor_1_rd, microprocessor_1_rx, microprocessor_1_ry;
  wire [9:0] microprocessor_1_address, microprocessor_1_pointer;
  wire [31:0] microprocessor_1_imm, microprocessor_1_rx_2, microprocessor_1_ry_2, microprocessor_1_s,
       microprocessor_1_storedata, ram_1_data, ram_2_data;

  Clock CLK (.out(CLK_out));
  RAM #(.addrWidth(10), .dataWidth(32)) ram_1 (
    .addr(microprocessor_1_address), .data(ram_1_data), .clk(CLK_out));  // open: sel, ld, clr
  not not_1 (not_1_out, microprocessor_1_store);
  microprocessor microprocessor_1 (
    .CLK(CLK_out), .Rx_2(microprocessor_1_rx_2), .Ry_2(microprocessor_1_ry_2), .overflow(OVERFLOW),
    .zero(ZERO), .CLR(CLR), .address(microprocessor_1_address), .WORD(ram_1_data), .Rx(microprocessor_1_rx),
    .IMM(microprocessor_1_imm), .Ry(microprocessor_1_ry), .Rd(microprocessor_1_rd), .opcode(OpCode),
    .S(microprocessor_1_s), .LOAD_STORE_DATA(ram_2_data), .pointer(microprocessor_1_pointer),
    .store(microprocessor_1_store), .StoreData(microprocessor_1_storedata));
  RAM #(.addrWidth(10), .dataWidth(32)) ram_2 (
    .addr(microprocessor_1_pointer), .data(ram_2_data), .clk(CLK_out), .ld(not_1_out));  // open: sel, clr
  assign ram_2_data = microprocessor_1_store ? microprocessor_1_storedata : 32'bz;  // Controlled_Buffer controlled_buffer_1
  // Probe on microprocessor_1_rd
  // Probe on microprocessor_1_rx
  // Probe on microprocessor_1_ry
  // Probe on microprocessor_1_rx_2
  // Probe on microprocessor_1_ry_2
  // Probe on microprocessor_1_imm
  // Probe on microprocessor_1_s
endmodule

module microprocessor (
  input  [31:0] WORD,
  input  CLK,
  input  [31:0] LOAD_STORE_DATA,
  input  CLR,
  output store,
  output [31:0] S,
  output [9:0] pointer,
  output overflow,
  output zero,
  output [31:0] StoreData,
  output [4:0] opcode,
  output [4:0] Rd,
  output [4:0] Rx,
  output [4:0] Ry,
  output [31:0] Rx_2,
  output [9:0] address,
  output [31:0] Ry_2,
  output [31:0] IMM
);

  wire and_1_out, atom_control_unit_1_out_2, not_1_out;
  wire [31:0] atom_load_1_out_2, multiplexer_1_out;

  molecule_read_data molecule_read_data_1 (.data(WORD), .Ry(Ry), .imm(IMM), .Rx(Rx), .Rd(Rd), .opcode(opcode));
  and and_1 (and_1_out, ~store, CLK);  // AND_Gate
  not not_1 (not_1_out, CLK);
  atom_pc atom_pc_1 (
    .clk(not_1_out), .step(10'h1), .clr(CLR), .address(address), .opcode(opcode), .imm(IMM), .zero(zero));
  atom_load atom_load_1 (.out(S), .data(LOAD_STORE_DATA), .OUT_2(atom_load_1_out_2), .opcode(opcode));
  molecule_registers molecule_registers_1 (
    .data_in(atom_load_1_out_2), .write(and_1_out), .sel_w(Rd), .x(Rx_2), .y(Ry_2), .sel_x(Rx), .sel_y(Ry),
    .d(StoreData));
  Multiplexer #(.width(32), .enable("false")) multiplexer_1 (
    .in0(Ry_2), .in1(IMM), .out(multiplexer_1_out), .sel(atom_control_unit_1_out_2));
  atom_control_unit atom_control_unit_1 (.opcode(opcode), .out_2(atom_control_unit_1_out_2));
  molecule_32bits molecule_32bits_1 (
    .Sel(opcode), .a(Rx_2), .overflow(overflow), .b(multiplexer_1_out), .S(S), .zero(zero));
  atom_store atom_store_1 (.out_2(store), .opcode(opcode));
  atom_32_to_10 atom_32_to_10_1 (.in(S), .out(pointer));

  // Other names for the same wires on the sheet: d[31:0] = StoreData
endmodule

module organism_ula (
  input  [31:0] a,
  input  [31:0] b,
  input  [4:0] Sel,
  output [31:0] S
);

  wire molecule_32bits_1_overflow, molecule_32bits_1_zero;

  molecule_32bits molecule_32bits_1 (
    .Sel(Sel), .a(a), .overflow(molecule_32bits_1_overflow), .b(b), .S(S), .zero(molecule_32bits_1_zero));
  LED overflow (.in(molecule_32bits_1_overflow));
  LED zero (.in(molecule_32bits_1_zero));
endmodule

module molecule_32bits (
  input  [4:0] Sel,
  input  [31:0] a,
  input  [31:0] b,
  output overflow,
  output [31:0] S,
  output zero
);

  wire atom_core_1_out, atom_core_1_send, atom_core_2_out, atom_core_2_send, atom_core_3_out,
       atom_core_3_send, atom_core_4_out, atom_core_4_send, atom_core_5_out, atom_core_5_send,
       atom_core_6_out, atom_core_6_send, atom_core_7_out, atom_core_7_send, atom_core_8_out,
       atom_core_8_send, atom_core_9_out, atom_core_9_send, atom_core_10_out, atom_core_10_send,
       atom_core_11_out, atom_core_11_send, atom_core_12_out, atom_core_12_send, atom_core_13_out,
       atom_core_13_send, atom_core_14_out, atom_core_14_send, atom_core_15_out, atom_core_15_send,
       atom_core_16_out, atom_core_16_send, atom_core_17_out, atom_core_17_send, atom_core_18_out,
       atom_core_18_send, atom_core_19_out, atom_core_19_send, atom_core_20_out, atom_core_20_send,
       atom_core_21_out, atom_core_21_send, atom_core_22_out, atom_core_22_send, atom_core_23_out,
       atom_core_23_send, atom_core_24_out, atom_core_24_send, atom_core_25_out, atom_core_25_send,
       atom_core_26_out, atom_core_26_send, atom_core_27_out, atom_core_27_send, atom_core_28_out,
       atom_core_28_send, atom_core_29_out, atom_core_29_send, atom_core_30_out, atom_core_30_send,
       atom_core_31_out, atom_core_31_send, atom_core_32_out, atom_core_32_send, atom_msb_1_receive;
  wire [31:0] atom_core_32_s;

  atom_zero atom_zero_1 (.a(S), .zero(zero));
  atom_slt atom_slt_1 (.s(atom_core_32_s), .r(S), .opcode(Sel), .a(a), .b(b));
  atom_msb atom_msb_1 (.opcode(Sel), .a(a[31]), .receive(atom_msb_1_receive), .lost(atom_core_32_send));
  atom_overflow atom_overflow_1 (
    .overflow_2(overflow), .a(a[31]), .b(b[31]), .s(atom_core_32_s[31]), .overflow(atom_core_1_out),
    .opcode(Sel));
  atom_core atom_core_1 (
    .a(a[31]), .b(b[31]), .in(atom_core_3_out), .out(atom_core_1_out), .opcode(Sel),
    .receive(atom_msb_1_receive), .send(atom_core_1_send), .s(atom_core_32_s[31]), .lost(1'b0));
  atom_core atom_core_2 (
    .a(a[29]), .b(b[29]), .in(atom_core_4_out), .out(atom_core_2_out), .opcode(Sel),
    .receive(atom_core_3_send), .send(atom_core_2_send), .s(atom_core_32_s[29]), .lost(1'b0));
  atom_core atom_core_3 (
    .a(a[30]), .b(b[30]), .in(atom_core_2_out), .out(atom_core_3_out), .opcode(Sel),
    .receive(atom_core_1_send), .send(atom_core_3_send), .s(atom_core_32_s[30]), .lost(1'b0));
  atom_core atom_core_4 (
    .a(a[28]), .b(b[28]), .in(atom_core_5_out), .out(atom_core_4_out), .opcode(Sel),
    .receive(atom_core_2_send), .send(atom_core_4_send), .s(atom_core_32_s[28]), .lost(1'b0));
  atom_core atom_core_5 (
    .a(a[27]), .b(b[27]), .in(atom_core_6_out), .out(atom_core_5_out), .opcode(Sel),
    .receive(atom_core_4_send), .send(atom_core_5_send), .s(atom_core_32_s[27]), .lost(1'b0));
  atom_core atom_core_6 (
    .a(a[26]), .b(b[26]), .in(atom_core_7_out), .out(atom_core_6_out), .opcode(Sel),
    .receive(atom_core_5_send), .send(atom_core_6_send), .s(atom_core_32_s[26]), .lost(1'b0));
  atom_core atom_core_7 (
    .a(a[25]), .b(b[25]), .in(atom_core_8_out), .out(atom_core_7_out), .opcode(Sel),
    .receive(atom_core_6_send), .send(atom_core_7_send), .s(atom_core_32_s[25]), .lost(1'b0));
  atom_core atom_core_8 (
    .a(a[24]), .b(b[24]), .in(atom_core_9_out), .out(atom_core_8_out), .opcode(Sel),
    .receive(atom_core_7_send), .send(atom_core_8_send), .s(atom_core_32_s[24]), .lost(1'b0));
  atom_core atom_core_9 (
    .a(a[23]), .b(b[23]), .in(atom_core_11_out), .out(atom_core_9_out), .opcode(Sel),
    .receive(atom_core_8_send), .send(atom_core_9_send), .s(atom_core_32_s[23]), .lost(1'b0));
  atom_core atom_core_10 (
    .a(a[21]), .b(b[21]), .in(atom_core_12_out), .out(atom_core_10_out), .opcode(Sel),
    .receive(atom_core_11_send), .send(atom_core_10_send), .s(atom_core_32_s[21]), .lost(1'b0));
  atom_core atom_core_11 (
    .a(a[22]), .b(b[22]), .in(atom_core_10_out), .out(atom_core_11_out), .opcode(Sel),
    .receive(atom_core_9_send), .send(atom_core_11_send), .s(atom_core_32_s[22]), .lost(1'b0));
  atom_core atom_core_12 (
    .a(a[20]), .b(b[20]), .in(atom_core_13_out), .out(atom_core_12_out), .opcode(Sel),
    .receive(atom_core_10_send), .send(atom_core_12_send), .s(atom_core_32_s[20]), .lost(1'b0));
  atom_core atom_core_13 (
    .a(a[19]), .b(b[19]), .in(atom_core_14_out), .out(atom_core_13_out), .opcode(Sel),
    .receive(atom_core_12_send), .send(atom_core_13_send), .s(atom_core_32_s[19]), .lost(1'b0));
  atom_core atom_core_14 (
    .a(a[18]), .b(b[18]), .in(atom_core_15_out), .out(atom_core_14_out), .opcode(Sel),
    .receive(atom_core_13_send), .send(atom_core_14_send), .s(atom_core_32_s[18]), .lost(1'b0));
  atom_core atom_core_15 (
    .a(a[17]), .b(b[17]), .in(atom_core_16_out), .out(atom_core_15_out), .opcode(Sel),
    .receive(atom_core_14_send), .send(atom_core_15_send), .s(atom_core_32_s[17]), .lost(1'b0));
  atom_core atom_core_16 (
    .a(a[16]), .b(b[16]), .in(atom_core_17_out), .out(atom_core_16_out), .opcode(Sel),
    .receive(atom_core_15_send), .send(atom_core_16_send), .s(atom_core_32_s[16]), .lost(1'b0));
  atom_core atom_core_17 (
    .a(a[15]), .b(b[15]), .in(atom_core_19_out), .out(atom_core_17_out), .opcode(Sel),
    .receive(atom_core_16_send), .send(atom_core_17_send), .s(atom_core_32_s[15]), .lost(1'b0));
  atom_core atom_core_18 (
    .a(a[13]), .b(b[13]), .in(atom_core_20_out), .out(atom_core_18_out), .opcode(Sel),
    .receive(atom_core_19_send), .send(atom_core_18_send), .s(atom_core_32_s[13]), .lost(1'b0));
  atom_core atom_core_19 (
    .a(a[14]), .b(b[14]), .in(atom_core_18_out), .out(atom_core_19_out), .opcode(Sel),
    .receive(atom_core_17_send), .send(atom_core_19_send), .s(atom_core_32_s[14]), .lost(1'b0));
  atom_core atom_core_20 (
    .a(a[12]), .b(b[12]), .in(atom_core_21_out), .out(atom_core_20_out), .opcode(Sel),
    .receive(atom_core_18_send), .send(atom_core_20_send), .s(atom_core_32_s[12]), .lost(1'b0));
  atom_core atom_core_21 (
    .a(a[11]), .b(b[11]), .in(atom_core_22_out), .out(atom_core_21_out), .opcode(Sel),
    .receive(atom_core_20_send), .send(atom_core_21_send), .s(atom_core_32_s[11]), .lost(1'b0));
  atom_core atom_core_22 (
    .a(a[10]), .b(b[10]), .in(atom_core_23_out), .out(atom_core_22_out), .opcode(Sel),
    .receive(atom_core_21_send), .send(atom_core_22_send), .s(atom_core_32_s[10]), .lost(1'b0));
  atom_core atom_core_23 (
    .a(a[9]), .b(b[9]), .in(atom_core_24_out), .out(atom_core_23_out), .opcode(Sel),
    .receive(atom_core_22_send), .send(atom_core_23_send), .s(atom_core_32_s[9]), .lost(1'b0));
  atom_core atom_core_24 (
    .a(a[8]), .b(b[8]), .in(atom_core_25_out), .out(atom_core_24_out), .opcode(Sel),
    .receive(atom_core_23_send), .send(atom_core_24_send), .s(atom_core_32_s[8]), .lost(1'b0));
  atom_core atom_core_25 (
    .a(a[7]), .b(b[7]), .in(atom_core_27_out), .out(atom_core_25_out), .opcode(Sel),
    .receive(atom_core_24_send), .send(atom_core_25_send), .s(atom_core_32_s[7]), .lost(1'b0));
  atom_core atom_core_26 (
    .a(a[5]), .b(b[5]), .in(atom_core_28_out), .out(atom_core_26_out), .opcode(Sel),
    .receive(atom_core_27_send), .send(atom_core_26_send), .s(atom_core_32_s[5]), .lost(1'b0));
  atom_core atom_core_27 (
    .a(a[6]), .b(b[6]), .in(atom_core_26_out), .out(atom_core_27_out), .opcode(Sel),
    .receive(atom_core_25_send), .send(atom_core_27_send), .s(atom_core_32_s[6]), .lost(1'b0));
  atom_core atom_core_28 (
    .a(a[4]), .b(b[4]), .in(atom_core_29_out), .out(atom_core_28_out), .opcode(Sel),
    .receive(atom_core_26_send), .send(atom_core_28_send), .s(atom_core_32_s[4]), .lost(1'b0));
  atom_core atom_core_29 (
    .a(a[3]), .b(b[3]), .in(atom_core_30_out), .out(atom_core_29_out), .opcode(Sel),
    .receive(atom_core_28_send), .send(atom_core_29_send), .s(atom_core_32_s[3]), .lost(1'b0));
  atom_core atom_core_30 (
    .a(a[2]), .b(b[2]), .in(atom_core_31_out), .out(atom_core_30_out), .opcode(Sel),
    .receive(atom_core_29_send), .send(atom_core_30_send), .s(atom_core_32_s[2]), .lost(1'b0));
  atom_core atom_core_31 (
    .a(a[1]), .b(b[1]), .in(atom_core_32_out), .out(atom_core_31_out), .opcode(Sel),
    .receive(atom_core_30_send), .send(atom_core_31_send), .s(atom_core_32_s[1]), .lost(1'b0));
  atom_core atom_core_32 (
    .a(a[0]), .b(b[0]), .in(1'b0), .out(atom_core_32_out), .opcode(Sel), .receive(atom_core_31_send),
    .send(atom_core_32_send), .s(atom_core_32_s[0]), .lost(atom_core_1_out));
endmodule

module molecule_registers (
  input  [31:0] data_in,
  input  write,
  input  [4:0] sel_w,
  input  [4:0] sel_x,
  input  [4:0] sel_y,
  output [31:0] x,
  output [31:0] y,
  output [31:0] d
);

  wire demultiplexer_1_out0, demultiplexer_1_out1, demultiplexer_1_out2, demultiplexer_1_out3,
       demultiplexer_1_out4, demultiplexer_1_out5, demultiplexer_1_out6, demultiplexer_1_out7,
       demultiplexer_1_out8, demultiplexer_1_out9, demultiplexer_1_out10, demultiplexer_1_out11,
       demultiplexer_1_out12, demultiplexer_1_out13, demultiplexer_1_out14, demultiplexer_1_out15,
       demultiplexer_1_out16, demultiplexer_1_out17, demultiplexer_1_out18, demultiplexer_1_out19,
       demultiplexer_1_out20, demultiplexer_1_out21, demultiplexer_1_out22, demultiplexer_1_out23,
       demultiplexer_1_out24, demultiplexer_1_out25, demultiplexer_1_out26, demultiplexer_1_out27,
       demultiplexer_1_out28, demultiplexer_1_out29, demultiplexer_1_out30, demultiplexer_1_out31;
  wire [31:0] atom_register_1_data_out, atom_register_2_data_out, atom_register_3_data_out,
       atom_register_4_data_out, atom_register_5_data_out, atom_register_6_data_out,
       atom_register_7_data_out, atom_register_8_data_out, atom_register_9_data_out,
       atom_register_10_data_out, atom_register_11_data_out, atom_register_12_data_out,
       atom_register_13_data_out, atom_register_14_data_out, atom_register_15_data_out,
       atom_register_16_data_out, atom_register_17_data_out, atom_register_18_data_out,
       atom_register_19_data_out, atom_register_20_data_out, atom_register_21_data_out,
       atom_register_22_data_out, atom_register_23_data_out, atom_register_24_data_out,
       atom_register_25_data_out, atom_register_26_data_out, atom_register_27_data_out,
       atom_register_28_data_out, atom_register_29_data_out, atom_register_30_data_out,
       atom_register_31_data_out, atom_register_32_data_out;

  Demultiplexer #(.select(5), .enable("false")) demultiplexer_1 (
    .out0(demultiplexer_1_out0), .out1(demultiplexer_1_out1), .out2(demultiplexer_1_out2),
    .out3(demultiplexer_1_out3), .out4(demultiplexer_1_out4), .out5(demultiplexer_1_out5),
    .out6(demultiplexer_1_out6), .out7(demultiplexer_1_out7), .out8(demultiplexer_1_out8),
    .out9(demultiplexer_1_out9), .out10(demultiplexer_1_out10), .out11(demultiplexer_1_out11),
    .out12(demultiplexer_1_out12), .out13(demultiplexer_1_out13), .out14(demultiplexer_1_out14),
    .out15(demultiplexer_1_out15), .out16(demultiplexer_1_out16), .out17(demultiplexer_1_out17),
    .out18(demultiplexer_1_out18), .out19(demultiplexer_1_out19), .out20(demultiplexer_1_out20),
    .out21(demultiplexer_1_out21), .out22(demultiplexer_1_out22), .out23(demultiplexer_1_out23),
    .out24(demultiplexer_1_out24), .out25(demultiplexer_1_out25), .out26(demultiplexer_1_out26),
    .out27(demultiplexer_1_out27), .out28(demultiplexer_1_out28), .out29(demultiplexer_1_out29),
    .out30(demultiplexer_1_out30), .out31(demultiplexer_1_out31), .in(write), .sel(sel_w));
  atom_register atom_register_1 (.clk(demultiplexer_1_out0), .data_in(data_in), .data_out(atom_register_1_data_out));
  atom_register atom_register_2 (.clk(demultiplexer_1_out1), .data_in(data_in), .data_out(atom_register_2_data_out));
  atom_register atom_register_3 (.clk(demultiplexer_1_out2), .data_in(data_in), .data_out(atom_register_3_data_out));
  atom_register atom_register_4 (.clk(demultiplexer_1_out3), .data_in(data_in), .data_out(atom_register_4_data_out));
  atom_register atom_register_5 (.clk(demultiplexer_1_out4), .data_in(data_in), .data_out(atom_register_5_data_out));
  atom_register atom_register_6 (.clk(demultiplexer_1_out5), .data_in(data_in), .data_out(atom_register_6_data_out));
  atom_register atom_register_7 (.clk(demultiplexer_1_out6), .data_in(data_in), .data_out(atom_register_7_data_out));
  atom_register atom_register_8 (.clk(demultiplexer_1_out7), .data_in(data_in), .data_out(atom_register_8_data_out));
  atom_register atom_register_9 (.clk(demultiplexer_1_out8), .data_in(data_in), .data_out(atom_register_9_data_out));
  atom_register atom_register_10 (.clk(demultiplexer_1_out9), .data_in(data_in), .data_out(atom_register_10_data_out));
  atom_register atom_register_11 (.clk(demultiplexer_1_out10), .data_in(data_in), .data_out(atom_register_11_data_out));
  atom_register atom_register_12 (.clk(demultiplexer_1_out11), .data_in(data_in), .data_out(atom_register_12_data_out));
  atom_register atom_register_13 (.clk(demultiplexer_1_out12), .data_in(data_in), .data_out(atom_register_13_data_out));
  atom_register atom_register_14 (.clk(demultiplexer_1_out13), .data_in(data_in), .data_out(atom_register_14_data_out));
  atom_register atom_register_15 (.clk(demultiplexer_1_out14), .data_in(data_in), .data_out(atom_register_15_data_out));
  atom_register atom_register_16 (.clk(demultiplexer_1_out15), .data_in(data_in), .data_out(atom_register_16_data_out));
  atom_register atom_register_17 (.clk(demultiplexer_1_out16), .data_in(data_in), .data_out(atom_register_17_data_out));
  atom_register atom_register_18 (.clk(demultiplexer_1_out17), .data_in(data_in), .data_out(atom_register_18_data_out));
  atom_register atom_register_19 (.clk(demultiplexer_1_out18), .data_in(data_in), .data_out(atom_register_19_data_out));
  atom_register atom_register_20 (.clk(demultiplexer_1_out19), .data_in(data_in), .data_out(atom_register_20_data_out));
  atom_register atom_register_21 (.clk(demultiplexer_1_out20), .data_in(data_in), .data_out(atom_register_21_data_out));
  atom_register atom_register_22 (.clk(demultiplexer_1_out21), .data_in(data_in), .data_out(atom_register_22_data_out));
  atom_register atom_register_23 (.clk(demultiplexer_1_out22), .data_in(data_in), .data_out(atom_register_23_data_out));
  atom_register atom_register_24 (.clk(demultiplexer_1_out23), .data_in(data_in), .data_out(atom_register_24_data_out));
  atom_register atom_register_25 (.clk(demultiplexer_1_out24), .data_in(data_in), .data_out(atom_register_25_data_out));
  atom_register atom_register_26 (.clk(demultiplexer_1_out25), .data_in(data_in), .data_out(atom_register_26_data_out));
  atom_register atom_register_27 (.clk(demultiplexer_1_out26), .data_in(data_in), .data_out(atom_register_27_data_out));
  atom_register atom_register_28 (.clk(demultiplexer_1_out27), .data_in(data_in), .data_out(atom_register_28_data_out));
  atom_register atom_register_29 (.clk(demultiplexer_1_out28), .data_in(data_in), .data_out(atom_register_29_data_out));
  atom_register atom_register_30 (.clk(demultiplexer_1_out29), .data_in(data_in), .data_out(atom_register_30_data_out));
  atom_register atom_register_31 (.clk(demultiplexer_1_out30), .data_in(data_in), .data_out(atom_register_31_data_out));
  atom_register atom_register_32 (.clk(demultiplexer_1_out31), .data_in(data_in), .data_out(atom_register_32_data_out));
  Multiplexer #(.select(5), .width(32), .enable("false")) multiplexer_1 (
    .in0(atom_register_1_data_out), .in1(atom_register_2_data_out), .in2(atom_register_3_data_out),
    .in3(atom_register_4_data_out), .in4(atom_register_5_data_out), .in5(atom_register_6_data_out),
    .in6(atom_register_7_data_out), .in7(atom_register_8_data_out), .in8(atom_register_9_data_out),
    .in9(atom_register_10_data_out), .in10(atom_register_11_data_out), .in11(atom_register_12_data_out),
    .in12(atom_register_13_data_out), .in13(atom_register_14_data_out), .in14(atom_register_15_data_out),
    .in15(atom_register_16_data_out), .in16(atom_register_17_data_out), .in17(atom_register_18_data_out),
    .in18(atom_register_19_data_out), .in19(atom_register_20_data_out), .in20(atom_register_21_data_out),
    .in21(atom_register_22_data_out), .in22(atom_register_23_data_out), .in23(atom_register_24_data_out),
    .in24(atom_register_25_data_out), .in25(atom_register_26_data_out), .in26(atom_register_27_data_out),
    .in27(atom_register_28_data_out), .in28(atom_register_29_data_out), .in29(atom_register_30_data_out),
    .in30(atom_register_31_data_out), .in31(atom_register_32_data_out), .out(x), .sel(sel_x));
  Multiplexer #(.select(5), .width(32), .enable("false")) multiplexer_2 (
    .in0(atom_register_1_data_out), .in1(atom_register_2_data_out), .in2(atom_register_3_data_out),
    .in3(atom_register_4_data_out), .in4(atom_register_5_data_out), .in5(atom_register_6_data_out),
    .in6(atom_register_7_data_out), .in7(atom_register_8_data_out), .in8(atom_register_9_data_out),
    .in9(atom_register_10_data_out), .in10(atom_register_11_data_out), .in11(atom_register_12_data_out),
    .in12(atom_register_13_data_out), .in13(atom_register_14_data_out), .in14(atom_register_15_data_out),
    .in15(atom_register_16_data_out), .in16(atom_register_17_data_out), .in17(atom_register_18_data_out),
    .in18(atom_register_19_data_out), .in19(atom_register_20_data_out), .in20(atom_register_21_data_out),
    .in21(atom_register_22_data_out), .in22(atom_register_23_data_out), .in23(atom_register_24_data_out),
    .in24(atom_register_25_data_out), .in25(atom_register_26_data_out), .in26(atom_register_27_data_out),
    .in27(atom_register_28_data_out), .in28(atom_register_29_data_out), .in29(atom_register_30_data_out),
    .in30(atom_register_31_data_out), .in31(atom_register_32_data_out), .out(y), .sel(sel_y));
  Multiplexer #(.select(5), .width(32), .enable("false")) multiplexer_3 (
    .in0(atom_register_1_data_out), .in1(atom_register_2_data_out), .in2(atom_register_3_data_out),
    .in3(atom_register_4_data_out), .in4(atom_register_5_data_out), .in5(atom_register_6_data_out),
    .in6(atom_register_7_data_out), .in7(atom_register_8_data_out), .in8(atom_register_9_data_out),
    .in9(atom_register_10_data_out), .in10(atom_register_11_data_out), .in11(atom_register_12_data_out),
    .in12(atom_register_13_data_out), .in13(atom_register_14_data_out), .in14(atom_register_15_data_out),
    .in15(atom_register_16_data_out), .in16(atom_register_17_data_out), .in17(atom_register_18_data_out),
    .in18(atom_register_19_data_out), .in19(atom_register_20_data_out), .in20(atom_register_21_data_out),
    .in21(atom_register_22_data_out), .in22(atom_register_23_data_out), .in23(atom_register_24_data_out),
    .in24(atom_register_25_data_out), .in25(atom_register_26_data_out), .in26(atom_register_27_data_out),
    .in27(atom_register_28_data_out), .in28(atom_register_29_data_out), .in29(atom_register_30_data_out),
    .in30(atom_register_31_data_out), .in31(atom_register_32_data_out), .out(d), .sel(sel_w));
endmodule

module molecule_read_data (
  input  [31:0] data,
  output [4:0] Ry,
  output [31:0] imm,
  output [4:0] Rx,
  output [4:0] Rd,
  output [4:0] opcode
);


  assign imm = {{21{data[11]}}, data[10:0]};
  assign opcode = data[31:27];
  assign Rd = data[26:22];
  assign Rx = data[21:17];
  assign Ry = data[16:12];
endmodule

module atom_core (
  input  [4:0] opcode,
  input  a,
  input  b,
  input  receive,
  input  in,
  input  lost,
  output s,
  output send,
  output out
);

  wire adder_1_cout, adder_1_out, and_1_out, nand_1_out, or_1_out, or_2_out, subtractor_1_bout,
       subtractor_1_out, xor_1_out;

  and and_1 (and_1_out, a, b);
  or or_1 (or_1_out, a, b);
  Adder #(.width(1)) adder_1 (.a(a), .b(b), .out(adder_1_out), .cin(in), .cout(adder_1_cout));
  Subtractor #(.width(1)) subtractor_1 (.a(a), .b(b), .out(subtractor_1_out), .bin(in), .bout(subtractor_1_bout));
  or or_2 (or_2_out, in, lost);
  nand nand_1 (nand_1_out, a, b);
  xor xor_1 (xor_1_out, a, b);
  Multiplexer #(.select(5), .enable("false")) multiplexer_1 (
    .in0(and_1_out), .in1(or_1_out), .in2(nand_1_out), .in3(xor_1_out), .in4(adder_1_out), .in5(adder_1_out),
    .in6(subtractor_1_out), .in7(in), .in8(receive), .in9(receive), .in10(or_2_out), .in11(receive),
    .in12(1'b0), .in13(subtractor_1_out), .in14(subtractor_1_out), .in15(1'b0), .in16(and_1_out),
    .in17(or_1_out), .in18(nand_1_out), .in19(xor_1_out), .in20(adder_1_out), .in21(adder_1_out),
    .in22(subtractor_1_out), .in23(1'b0), .in24(1'b0), .in25(1'b0), .in26(1'b0), .in27(1'b0), .in28(1'b0),
    .in29(adder_1_out), .in30(adder_1_out), .in31(1'b0), .out(s), .sel(opcode));
  Multiplexer #(.select(5), .enable("false")) multiplexer_2 (
    .in0(1'b0), .in1(1'b0), .in2(1'b0), .in3(1'b0), .in4(adder_1_cout), .in5(adder_1_cout),
    .in6(subtractor_1_bout), .in7(a), .in8(1'b0), .in9(1'b0), .in10(a), .in11(1'b0), .in12(1'b0),
    .in13(subtractor_1_bout), .in14(subtractor_1_bout), .in15(1'b0), .in16(1'b0), .in17(1'b0), .in18(1'b0),
    .in19(1'b0), .in20(adder_1_cout), .in21(adder_1_cout), .in22(subtractor_1_bout), .in23(1'b0),
    .in24(1'b0), .in25(1'b0), .in26(1'b0), .in27(1'b0), .in28(1'b0), .in29(adder_1_cout),
    .in30(adder_1_cout), .in31(1'b0), .out(out), .sel(opcode));
  Multiplexer #(.select(5), .enable("false")) multiplexer_3 (
    .in0(1'b0), .in1(1'b0), .in2(1'b0), .in3(1'b0), .in4(1'b0), .in5(1'b0), .in6(1'b0), .in7(1'b0), .in8(a),
    .in9(a), .in10(1'b0), .in11(a), .in12(1'b0), .in13(1'b0), .in14(1'b0), .in15(1'b0), .in16(1'b0),
    .in17(1'b0), .in18(1'b0), .in19(1'b0), .in20(1'b0), .in21(1'b0), .in22(1'b0), .in23(1'b0), .in24(a),
    .in25(a), .in26(1'b0), .in27(a), .in28(1'b0), .in29(1'b0), .in30(1'b0), .in31(1'b0), .out(send),
    .sel(opcode));
endmodule

module atom_overflow (
  input  [4:0] opcode,
  input  a,
  input  b,
  input  s,
  input  overflow,
  output overflow_2
);

  wire and_1_out, and_2_out, and_3_out, not_1_out, not_2_out, not_3_out, or_1_out;

  and and_1 (and_1_out, ~opcode[3], opcode[2], ~opcode[1], ~opcode[0]);  // AND_Gate
  Multiplexer #(.enable("false")) multiplexer_1 (.in0(overflow), .in1(or_1_out), .out(overflow_2), .sel(and_1_out));
  or or_1 (or_1_out, and_2_out, and_3_out);
  and and_2 (and_2_out, not_1_out, not_2_out, s);
  and and_3 (and_3_out, a, b, not_3_out);
  not not_1 (not_1_out, a);
  not not_2 (not_2_out, b);
  not not_3 (not_3_out, s);
endmodule

module atom_zero (
  input  [31:0] a,
  output zero
);

  and and_1 (zero, ~a[31], ~a[30], ~a[29], ~a[28], ~a[27], ~a[26], ~a[25], ~a[24], ~a[23], ~a[22], ~a[21], ~a[20], ~a[19], ~a[18], ~a[17], ~a[16], ~a[15], ~a[14], ~a[13], ~a[12], ~a[11], ~a[10], ~a[9], ~a[8], ~a[7], ~a[6], ~a[5], ~a[4], ~a[3], ~a[2], ~a[1], ~a[0]);  // AND_Gate
endmodule

module atom_msb (
  input  [4:0] opcode,
  input  a,
  input  lost,
  output receive
);

  wire and_1_out, and_2_out;

  and and_1 (and_1_out, opcode[3], ~opcode[2], ~opcode[1], opcode[0], a);  // AND_Gate
  and and_2 (and_2_out, opcode[3], ~opcode[2], opcode[1], opcode[0], lost);  // AND_Gate
  or or_1 (receive, and_1_out, and_2_out);
endmodule

module atom_slt (
  input  [4:0] opcode,
  input  [31:0] s,
  input  [31:0] a,
  input  [31:0] b,
  output [31:0] r
);

  wire and_2_out;
  wire [0:0] and_1_out;
  wire [31:0] subtractor_1_out;

  Subtractor #(.width(32)) subtractor_1 (.a(a), .b(b), .out(subtractor_1_out));  // open: bin, bout
  and and_1 (and_1_out[0], subtractor_1_out[31], subtractor_1_out[31]);
  and and_2 (and_2_out, ~opcode[0], ~opcode[1], opcode[2], opcode[3]);  // AND_Gate
  Multiplexer #(.width(32), .enable("false")) multiplexer_1 (
    .in0(s), .in1({{31{1'b0}}, and_1_out[0]}), .out(r), .sel(and_2_out));
endmodule

module atom_register (
  input  clk,
  input  [31:0] data_in,
  output [31:0] data_out
);

  D_Flip_Flop d_ff_1 (.clk(clk), .D(data_in[0]), .Q(data_out[0]));  // open: Qn, preset, en, reset
  D_Flip_Flop d_ff_2 (.clk(clk), .D(data_in[1]), .Q(data_out[1]));  // open: Qn, preset, en, reset
  D_Flip_Flop d_ff_3 (.clk(clk), .D(data_in[2]), .Q(data_out[2]));  // open: Qn, preset, en, reset
  D_Flip_Flop d_ff_4 (.clk(clk), .D(data_in[3]), .Q(data_out[3]));  // open: Qn, preset, en, reset
  D_Flip_Flop d_ff_5 (.clk(clk), .D(data_in[4]), .Q(data_out[4]));  // open: Qn, preset, en, reset
  D_Flip_Flop d_ff_6 (.clk(clk), .D(data_in[5]), .Q(data_out[5]));  // open: Qn, preset, en, reset
  D_Flip_Flop d_ff_7 (.clk(clk), .D(data_in[6]), .Q(data_out[6]));  // open: Qn, preset, en, reset
  D_Flip_Flop d_ff_8 (.clk(clk), .D(data_in[7]), .Q(data_out[7]));  // open: Qn, preset, en, reset
  D_Flip_Flop d_ff_9 (.clk(clk), .D(data_in[8]), .Q(data_out[8]));  // open: Qn, preset, en, reset
  D_Flip_Flop d_ff_10 (.clk(clk), .D(data_in[9]), .Q(data_out[9]));  // open: Qn, preset, en, reset
  D_Flip_Flop d_ff_11 (.clk(clk), .D(data_in[10]), .Q(data_out[10]));  // open: Qn, preset, en, reset
  D_Flip_Flop d_ff_12 (.clk(clk), .D(data_in[11]), .Q(data_out[11]));  // open: Qn, preset, en, reset
  D_Flip_Flop d_ff_13 (.clk(clk), .D(data_in[12]), .Q(data_out[12]));  // open: Qn, preset, en, reset
  D_Flip_Flop d_ff_14 (.clk(clk), .D(data_in[13]), .Q(data_out[13]));  // open: Qn, preset, en, reset
  D_Flip_Flop d_ff_15 (.clk(clk), .D(data_in[14]), .Q(data_out[14]));  // open: Qn, preset, en, reset
  D_Flip_Flop d_ff_16 (.clk(clk), .D(data_in[15]), .Q(data_out[15]));  // open: Qn, preset, en, reset
  D_Flip_Flop d_ff_17 (.clk(clk), .D(data_in[16]), .Q(data_out[16]));  // open: Qn, preset, en, reset
  D_Flip_Flop d_ff_18 (.clk(clk), .D(data_in[17]), .Q(data_out[17]));  // open: Qn, preset, en, reset
  D_Flip_Flop d_ff_19 (.clk(clk), .D(data_in[18]), .Q(data_out[18]));  // open: Qn, preset, en, reset
  D_Flip_Flop d_ff_20 (.clk(clk), .D(data_in[19]), .Q(data_out[19]));  // open: Qn, preset, en, reset
  D_Flip_Flop d_ff_21 (.clk(clk), .D(data_in[20]), .Q(data_out[20]));  // open: Qn, preset, en, reset
  D_Flip_Flop d_ff_22 (.clk(clk), .D(data_in[21]), .Q(data_out[21]));  // open: Qn, preset, en, reset
  D_Flip_Flop d_ff_23 (.clk(clk), .D(data_in[22]), .Q(data_out[22]));  // open: Qn, preset, en, reset
  D_Flip_Flop d_ff_24 (.clk(clk), .D(data_in[23]), .Q(data_out[23]));  // open: Qn, preset, en, reset
  D_Flip_Flop d_ff_25 (.clk(clk), .D(data_in[24]), .Q(data_out[24]));  // open: Qn, preset, en, reset
  D_Flip_Flop d_ff_26 (.clk(clk), .D(data_in[25]), .Q(data_out[25]));  // open: Qn, preset, en, reset
  D_Flip_Flop d_ff_27 (.clk(clk), .D(data_in[26]), .Q(data_out[26]));  // open: Qn, preset, en, reset
  D_Flip_Flop d_ff_28 (.clk(clk), .D(data_in[27]), .Q(data_out[27]));  // open: Qn, preset, en, reset
  D_Flip_Flop d_ff_29 (.clk(clk), .D(data_in[28]), .Q(data_out[28]));  // open: Qn, preset, en, reset
  D_Flip_Flop d_ff_30 (.clk(clk), .D(data_in[29]), .Q(data_out[29]));  // open: Qn, preset, en, reset
  D_Flip_Flop d_ff_31 (.clk(clk), .D(data_in[30]), .Q(data_out[30]));  // open: Qn, preset, en, reset
  D_Flip_Flop d_ff_32 (.clk(clk), .D(data_in[31]), .Q(data_out[31]));  // open: Qn, preset, en, reset
endmodule

module atom_control_unit (
  input  [4:0] opcode,
  output out_2
);

  wire and_1_out, and_2_out, and_3_out, and_4_out, and_5_out, and_6_out, and_7_out, and_8_out, and_9_out,
       xor_1_out;

  and and_1 (and_1_out, opcode[4], ~opcode[3], ~opcode[2], ~opcode[1], ~opcode[0]);  // AND_Gate
  and and_2 (and_2_out, opcode[4], ~opcode[3], ~opcode[2], ~opcode[1], opcode[0]);  // AND_Gate
  and and_3 (and_3_out, opcode[4], ~opcode[3], ~opcode[2], opcode[1], ~opcode[0]);  // AND_Gate
  and and_4 (and_4_out, opcode[4], ~opcode[3], ~opcode[2], opcode[1], opcode[0]);  // AND_Gate
  and and_5 (and_5_out, opcode[4], ~opcode[3], opcode[2], ~opcode[1], ~opcode[0]);  // AND_Gate
  ExactlyOne xor_1 (
    .out(xor_1_out), .in0(and_1_out), .in1(and_2_out), .in2(and_3_out), .in3(and_4_out), .in4(and_5_out),
    .in5(and_6_out), .in6(and_8_out), .in7(and_7_out), .in8(and_9_out));
  Multiplexer #(.enable("false")) multiplexer_1 (.in0(1'b0), .in1(1'b1), .out(out_2), .sel(xor_1_out));
  and and_6 (and_6_out, opcode[4], ~opcode[3], opcode[2], ~opcode[1], opcode[0]);  // AND_Gate
  and and_7 (and_7_out, opcode[4], opcode[3], opcode[2], ~opcode[1], ~opcode[0]);  // AND_Gate
  and and_8 (and_8_out, opcode[4], ~opcode[3], opcode[2], opcode[1], ~opcode[0]);  // AND_Gate
  and and_9 (and_9_out, opcode[4], opcode[3], opcode[2], opcode[1], opcode[0]);
endmodule

module atom_pc (
  input  clk,
  input  clr,
  input  [9:0] step,
  input  [31:0] imm,
  input  [4:0] opcode,
  input  zero,
  output [9:0] address
);

  wire and_1_out, and_2_out, and_3_out, or_1_out;
  wire [9:0] adder_1_out, atom_32_to_10_1_out, multiplexer_1_out, multiplexer_2_out;

  Multiplexer #(.width(10), .enable("false")) multiplexer_1 (
    .in0(step), .in1(atom_32_to_10_1_out), .out(multiplexer_1_out), .sel(or_1_out));
  or or_1 (or_1_out, and_1_out, and_2_out);
  atom_32_to_10 atom_32_to_10_1 (.in(imm), .out(atom_32_to_10_1_out));
  Register #(.width(10)) register_1 (.D(multiplexer_2_out), .Q(address), .clk(clk), .clr(clr));  // open: en
  and and_1 (and_1_out, opcode[0], ~opcode[1], opcode[2], opcode[3], ~opcode[4], zero);  // AND_Gate
  and and_2 (and_2_out, ~opcode[0], opcode[1], opcode[2], opcode[3], ~opcode[4], ~zero);  // AND_Gate
  Adder #(.width(10)) adder_1 (.a(address), .b(multiplexer_1_out), .out(adder_1_out));  // open: cin, cout
  Multiplexer #(.width(10), .enable("false")) multiplexer_2 (
    .in0(adder_1_out), .in1(atom_32_to_10_1_out), .out(multiplexer_2_out), .sel(and_3_out));
  and and_3 (and_3_out, opcode[4], opcode[3], opcode[2], opcode[1], opcode[0]);
endmodule

module atom_32_to_10 (
  input  [31:0] in,
  output [9:0] out
);


  assign in[30:10] = {21{in[31]}};
  assign out = in[9:0];
  // also tied to GND on the sheet: in[31]
endmodule

module atom_load (
  input  [31:0] out,
  input  [31:0] data,
  input  [4:0] opcode,
  output [31:0] OUT_2
);

  wire and_1_out;

  Multiplexer #(.width(32), .enable("false")) multiplexer_1 (.in0(out), .in1(data), .out(OUT_2), .sel(and_1_out));
  and and_1 (and_1_out, opcode[4], opcode[3], opcode[2], ~opcode[1], opcode[0]);  // AND_Gate
endmodule

module atom_store (
  input  [4:0] opcode,
  output out_2
);

  and and_1 (out_2, opcode[4], opcode[3], opcode[2], opcode[1], ~opcode[0]);  // AND_Gate
endmodule
