// Logisim project ula.circ as structural Verilog: 8 circuits, main circuit organism
module organism (
  input  [31:0] a,
  input  [31:0] b,
  input  [4:0] Sel,
  output [31:0] S
);

  wire molecule_32bits_1_overflow, molecule_32bits_1_zero;

  molecule_32bits molecule_32bits_1 (
    .Sel(Sel), .a(a), .overflow(molecule_32bits_1_overflow), .b(b), .S(S), .zero(molecule_32bits_1_zero));
  LED overflow (.in(molecule_32bits_1_overflow));
  LED zero (.in(molecule_32bits_1_zero));
endmodule

module molecule_32bits (
  input  [4:0] Sel,
  input  [31:0] a,
  input  [31:0] b,
  output overflow,
  output [31:0] S,
  output zero
);

  wire atom_main_1_out, atom_main_1_send, atom_main_2_out, atom_main_2_send, atom_main_3_out,
       atom_main_3_send, atom_main_4_out, atom_main_4_send, atom_main_5_out, atom_main_5_send,
       atom_main_6_out, atom_main_6_send, atom_main_7_out, atom_main_7_send, atom_main_8_out,
       atom_main_8_send, atom_main_9_out, atom_main_9_send, atom_main_10_out, atom_main_10_send,
       atom_main_11_out, atom_main_11_send, atom_main_12_out, atom_main_12_send, atom_main_13_out,
       atom_main_13_send, atom_main_14_out, atom_main_14_send, atom_main_15_out, atom_main_15_send,
       atom_main_16_out, atom_main_16_send, atom_main_17_out, atom_main_17_send, atom_main_18_out,
       atom_main_18_send, atom_main_19_out, atom_main_19_send, atom_main_20_out, atom_main_20_send,
       atom_main_21_out, atom_main_21_send, atom_main_22_out, atom_main_22_send, atom_main_23_out,
       atom_main_23_send, atom_main_24_out, atom_main_24_send, atom_main_25_out, atom_main_25_send,
       atom_main_26_out, atom_main_26_send, atom_main_27_out, atom_main_27_send, atom_main_28_out,
       atom_main_28_send, atom_main_29_out, atom_main_29_send, atom_main_30_out, atom_main_30_send,
       atom_main_31_out, atom_main_31_send, atom_main_32_out, atom_main_32_send, atom_msb_1_receive;
  wire [31:0] atom_main_32_s;

  atom_zero atom_zero_1 (.a(S), .zero(zero));
  atom_slt atom_slt_1 (.s(atom_main_32_s), .slt(atom_main_2_out), .r(S), .opcode(Sel), .a_msb(a[31]), .b_msb(b[31]));
  atom_msb atom_msb_1 (.opcode(Sel), .a(a[31]), .receive(atom_msb_1_receive), .lost(atom_main_32_send));
  atom_overflow atom_overflow_1 (
    .overflow_2(overflow), .a(a[31]), .b(b[31]), .s(atom_main_32_s[31]), .overflow(atom_main_1_out),
    .opcode(Sel));
  atom_main atom_main_1 (
    .a(a[31]), .b(b[31]), .in(atom_main_3_out), .out(atom_main_1_out), .opcode(Sel),
    .receive(atom_msb_1_receive), .send(atom_main_1_send), .s(atom_main_32_s[31]), .lost(1'b0));
  atom_main atom_main_2 (
    .a(a[29]), .b(b[29]), .in(atom_main_4_out), .out(atom_main_2_out), .opcode(Sel),
    .receive(atom_main_3_send), .send(atom_main_2_send), .s(atom_main_32_s[29]), .lost(1'b0));
  atom_main atom_main_3 (
    .a(a[30]), .b(b[30]), .in(atom_main_2_out), .out(atom_main_3_out), .opcode(Sel),
    .receive(atom_main_1_send), .send(atom_main_3_send), .s(atom_main_32_s[30]), .lost(1'b0));
  atom_main atom_main_4 (
    .a(a[28]), .b(b[28]), .in(atom_main_5_out), .out(atom_main_4_out), .opcode(Sel),
    .receive(atom_main_2_send), .send(atom_main_4_send), .s(atom_main_32_s[28]), .lost(1'b0));
  atom_main atom_main_5 (
    .a(a[27]), .b(b[27]), .in(atom_main_6_out), .out(atom_main_5_out), .opcode(Sel),
    .receive(atom_main_4_send), .send(atom_main_5_send), .s(atom_main_32_s[27]), .lost(1'b0));
  atom_main atom_main_6 (
    .a(a[26]), .b(b[26]), .in(atom_main_7_out), .out(atom_main_6_out), .opcode(Sel),
    .receive(atom_main_5_send), .send(atom_main_6_send), .s(atom_main_32_s[26]), .lost(1'b0));
  atom_main atom_main_7 (
    .a(a[25]), .b(b[25]), .in(atom_main_8_out), .out(atom_main_7_out), .opcode(Sel),
    .receive(atom_main_6_send), .send(atom_main_7_send), .s(atom_main_32_s[25]), .lost(1'b0));
  atom_main atom_main_8 (
    .a(a[24]), .b(b[24]), .in(atom_main_9_out), .out(atom_main_8_out), .opcode(Sel),
    .receive(atom_main_7_send), .send(atom_main_8_send), .s(atom_main_32_s[24]), .lost(1'b0));
  atom_main atom_main_9 (
    .a(a[23]), .b(b[23]), .in(atom_main_11_out), .out(atom_main_9_out), .opcode(Sel),
    .receive(atom_main_8_send), .send(atom_main_9_send), .s(atom_main_32_s[23]), .lost(1'b0));
  atom_main atom_main_10 (
    .a(a[21]), .b(b[21]), .in(atom_main_12_out), .out(atom_main_10_out), .opcode(Sel),
    .receive(atom_main_11_send), .send(atom_main_10_send), .s(atom_main_32_s[21]), .lost(1'b0));
  atom_main atom_main_11 (
    .a(a[22]), .b(b[22]), .in(atom_main_10_out), .out(atom_main_11_out), .opcode(Sel),
    .receive(atom_main_9_send), .send(atom_main_11_send), .s(atom_main_32_s[22]), .lost(1'b0));
  atom_main atom_main_12 (
    .a(a[20]), .b(b[20]), .in(atom_main_13_out), .out(atom_main_12_out), .opcode(Sel),
    .receive(atom_main_10_send), .send(atom_main_12_send), .s(atom_main_32_s[20]), .lost(1'b0));
  atom_main atom_main_13 (
    .a(a[19]), .b(b[19]), .in(atom_main_14_out), .out(atom_main_13_out), .opcode(Sel),
    .receive(atom_main_12_send), .send(atom_main_13_send), .s(atom_main_32_s[19]), .lost(1'b0));
  atom_main atom_main_14 (
    .a(a[18]), .b(b[18]), .in(atom_main_15_out), .out(atom_main_14_out), .opcode(Sel),
    .receive(atom_main_13_send), .send(atom_main_14_send), .s(atom_main_32_s[18]), .lost(1'b0));
  atom_main atom_main_15 (
    .a(a[17]), .b(b[17]), .in(atom_main_16_out), .out(atom_main_15_out), .opcode(Sel),
    .receive(atom_main_14_send), .send(atom_main_15_send), .s(atom_main_32_s[17]), .lost(1'b0));
  atom_main atom_main_16 (
    .a(a[16]), .b(b[16]), .in(atom_main_17_out), .out(atom_main_16_out), .opcode(Sel),
    .receive(atom_main_15_send), .send(atom_main_16_send), .s(atom_main_32_s[16]), .lost(1'b0));
  atom_main atom_main_17 (
    .a(a[15]), .b(b[15]), .in(atom_main_18_out), .out(atom_main_17_out), .opcode(Sel),
    .receive(atom_main_16_send), .send(atom_main_17_send), .s(atom_main_32_s[15]), .lost(1'b0));
  atom_main atom_main_18 (
    .a(a[14]), .b(b[14]), .in(atom_main_19_out), .out(atom_main_18_out), .opcode(Sel),
    .receive(atom_main_17_send), .send(atom_main_18_send), .s(atom_main_32_s[14]), .lost(1'b0));
  atom_main atom_main_19 (
    .a(a[13]), .b(b[13]), .in(atom_main_20_out), .out(atom_main_19_out), .opcode(Sel),
    .receive(atom_main_18_send), .send(atom_main_19_send), .s(atom_main_32_s[13]), .lost(1'b0));
  atom_main atom_main_20 (
    .a(a[12]), .b(b[12]), .in(atom_main_21_out), .out(atom_main_20_out), .opcode(Sel),
    .receive(atom_main_19_send), .send(atom_main_20_send), .s(atom_main_32_s[12]), .lost(1'b0));
  atom_main atom_main_21 (
    .a(a[11]), .b(b[11]), .in(atom_main_22_out), .out(atom_main_21_out), .opcode(Sel),
    .receive(atom_main_20_send), .send(atom_main_21_send), .s(atom_main_32_s[11]), .lost(1'b0));
  atom_main atom_main_22 (
    .a(a[10]), .b(b[10]), .in(atom_main_23_out), .out(atom_main_22_out), .opcode(Sel),
    .receive(atom_main_21_send), .send(atom_main_22_send), .s(atom_main_32_s[10]), .lost(1'b0));
  atom_main atom_main_23 (
    .a(a[9]), .b(b[9]), .in(atom_main_24_out), .out(atom_main_23_out), .opcode(Sel),
    .receive(atom_main_22_send), .send(atom_main_23_send), .s(atom_main_32_s[9]), .lost(1'b0));
  atom_main atom_main_24 (
    .a(a[8]), .b(b[8]), .in(atom_main_25_out), .out(atom_main_24_out), .opcode(Sel),
    .receive(atom_main_23_send), .send(atom_main_24_send), .s(atom_main_32_s[8]), .lost(1'b0));
  atom_main atom_main_25 (
    .a(a[7]), .b(b[7]), .in(atom_main_26_out), .out(atom_main_25_out), .opcode(Sel),
    .receive(atom_main_24_send), .send(atom_main_25_send), .s(atom_main_32_s[7]), .lost(1'b0));
  atom_main atom_main_26 (
    .a(a[6]), .b(b[6]), .in(atom_main_27_out), .out(atom_main_26_out), .opcode(Sel),
    .receive(atom_main_25_send), .send(atom_main_26_send), .s(atom_main_32_s[6]), .lost(1'b0));
  atom_main atom_main_27 (
    .a(a[5]), .b(b[5]), .in(atom_main_28_out), .out(atom_main_27_out), .opcode(Sel),
    .receive(atom_main_26_send), .send(atom_main_27_send), .s(atom_main_32_s[5]), .lost(1'b0));
  atom_main atom_main_28 (
    .a(a[4]), .b(b[4]), .in(atom_main_29_out), .out(atom_main_28_out), .opcode(Sel),
    .receive(atom_main_27_send), .send(atom_main_28_send), .s(atom_main_32_s[4]), .lost(1'b0));
  atom_main atom_main_29 (
    .a(a[3]), .b(b[3]), .in(atom_main_30_out), .out(atom_main_29_out), .opcode(Sel),
    .receive(atom_main_28_send), .send(atom_main_29_send), .s(atom_main_32_s[3]), .lost(1'b0));
  atom_main atom_main_30 (
    .a(a[2]), .b(b[2]), .in(atom_main_31_out), .out(atom_main_30_out), .opcode(Sel),
    .receive(atom_main_29_send), .send(atom_main_30_send), .s(atom_main_32_s[2]), .lost(1'b0));
  atom_main atom_main_31 (
    .a(a[1]), .b(b[1]), .in(atom_main_32_out), .out(atom_main_31_out), .opcode(Sel),
    .receive(atom_main_30_send), .send(atom_main_31_send), .s(atom_main_32_s[1]), .lost(1'b0));
  atom_main atom_main_32 (
    .a(a[0]), .b(b[0]), .in(1'b0), .out(atom_main_32_out), .opcode(Sel), .receive(atom_main_31_send),
    .send(atom_main_32_send), .s(atom_main_32_s[0]), .lost(atom_main_1_out));
endmodule

module molecule_2bits (
  input  [4:0] in_1,
  input  [1:0] in_2,
  input  [1:0] in_3,
  input  in_4,
  output [1:0] out_5,
  output out_6
);

  wire atom_main_1_out, atom_main_1_send, atom_main_2_out, atom_main_2_send, atom_msb_1_receive, undriven;

  atom_msb atom_msb_1 (.opcode(in_1), .a(in_2[1]), .receive(atom_msb_1_receive), .lost(undriven));
  atom_overflow atom_overflow_1 (
    .overflow_2(out_6), .a(in_2[1]), .b(in_3[1]), .s(out_5[1]), .overflow(atom_main_1_out), .opcode(in_1));
  atom_main atom_main_1 (
    .a(in_2[1]), .b(in_3[1]), .in(atom_main_2_out), .out(atom_main_1_out), .opcode(in_1),
    .receive(atom_msb_1_receive), .send(atom_main_1_send), .s(out_5[1]), .lost(in_4));
  atom_main atom_main_2 (
    .a(in_2[0]), .b(in_3[0]), .in(in_4), .out(atom_main_2_out), .opcode(in_1), .receive(atom_main_1_send),
    .send(atom_main_2_send), .s(out_5[0]), .lost(undriven));
  LED led_1 (.in(atom_main_2_send));
endmodule

module atom_main (
  input  [4:0] opcode,
  input  a,
  input  b,
  input  receive,
  input  in,
  input  lost,
  output s,
  output send,
  output out
);

  wire adder_1_cout, adder_1_out, and_1_out, and_2_out, and_3_out, and_4_out, and_5_out, and_6_out,
       nand_1_out, or_1_out, or_2_out, or_3_out, or_4_out, subtractor_1_bout, subtractor_1_out, xor_1_out;

  and and_1 (and_1_out, a, b);
  or or_1 (or_1_out, a, b);
  Adder #(.width(1)) adder_1 (.a(a), .b(b), .out(adder_1_out), .cin(in), .cout(adder_1_cout));
  Subtractor #(.width(1)) subtractor_1 (.a(a), .b(b), .out(subtractor_1_out), .bin(in), .bout(subtractor_1_bout));
  or or_2 (or_2_out, in, lost);
  and and_2 (and_2_out, ~a, b);  // AND_Gate
  and and_3 (and_3_out, ~a, ~b);  // AND_Gate
  and and_4 (and_4_out, a, b);
  nand nand_1 (nand_1_out, a, b);
  xor xor_1 (xor_1_out, a, b);
  and and_5 (and_5_out, and_3_out, in);
  or or_3 (or_3_out, and_5_out, and_6_out);
  and and_6 (and_6_out, and_4_out, in);
  or or_4 (or_4_out, and_2_out, or_3_out);
  Multiplexer #(.select(5)) multiplexer_1 (
    .in0(and_1_out), .in1(or_1_out), .in2(nand_1_out), .in3(xor_1_out), .in4(adder_1_out), .in5(adder_1_out),
    .in6(subtractor_1_out), .in7(in), .in8(receive), .in9(receive), .in10(or_2_out), .in11(receive),
    .in12(or_4_out), .out(s), .sel(opcode));  // open: in13, in14, in15, in16, in17, in18, in19, in20, in21, in22, in23, in24, in25, in26, in27, in28, in29, in30, in31, en
  Multiplexer #(.select(5)) multiplexer_2 (
    .in0(1'b0), .in1(1'b0), .in2(1'b0), .in3(1'b0), .in4(adder_1_cout), .in5(adder_1_cout),
    .in6(subtractor_1_bout), .in7(a), .in8(1'b0), .in9(1'b0), .in10(a), .in11(1'b0), .in12(or_4_out),
    .in13(1'b0), .in14(1'b0), .in15(1'b0), .in16(1'b0), .in17(1'b0), .in18(1'b0), .in19(1'b0), .in20(1'b0),
    .in21(1'b0), .in22(1'b0), .in23(1'b0), .in24(1'b0), .in25(1'b0), .in26(1'b0), .in27(1'b0), .in28(1'b0),
    .in29(1'b0), .in30(1'b0), .in31(1'b0), .out(out), .sel(opcode));  // open: en
  Multiplexer #(.select(5)) multiplexer_3 (
    .in0(1'b0), .in1(1'b0), .in2(1'b0), .in3(1'b0), .in4(1'b0), .in5(1'b0), .in6(1'b0), .in7(1'b0), .in8(a),
    .in9(a), .in10(1'b0), .in11(a), .in12(1'b0), .in13(1'b0), .in14(1'b0), .in15(1'b0), .in16(1'b0),
    .in17(1'b0), .in18(1'b0), .in19(1'b0), .in20(1'b0), .in21(1'b0), .in22(1'b0), .in23(1'b0), .in24(1'b0),
    .in25(1'b0), .in26(1'b0), .in27(1'b0), .in28(1'b0), .in29(1'b0), .in30(1'b0), .in31(1'b0), .out(send),
    .sel(opcode));  // open: en
endmodule

module atom_overflow (
  input  [4:0] opcode,
  input  a,
  input  b,
  input  s,
  input  overflow,
  output overflow_2
);

  wire and_1_out, and_2_out, and_3_out, not_1_out, not_2_out, not_3_out, or_1_out;

  Multiplexer multiplexer_1 (.in0(overflow), .in1(or_1_out), .out(overflow_2), .sel(and_1_out));  // open: en
  and and_1 (and_1_out, ~opcode[4], ~opcode[3], opcode[2], ~opcode[1], ~opcode[0]);  // AND_Gate
  or or_1 (or_1_out, and_2_out, and_3_out);
  and and_2 (and_2_out, not_1_out, not_2_out, s);
  and and_3 (and_3_out, a, b, not_3_out);
  not not_1 (not_1_out, a);
  not not_2 (not_2_out, b);
  not not_3 (not_3_out, s);
endmodule

module atom_zero (
  input  [31:0] a,
  output zero
);

  and and_1 (zero, ~a[31], ~a[30], ~a[29], ~a[28], ~a[27], ~a[26], ~a[25], ~a[24], ~a[23], ~a[22], ~a[21], ~a[20], ~a[19], ~a[18], ~a[17], ~a[16], ~a[15], ~a[14], ~a[13], ~a[12], ~a[11], ~a[10], ~a[9], ~a[8], ~a[7], ~a[6], ~a[5], ~a[4], ~a[3], ~a[2], ~a[1], ~a[0]);  // AND_Gate
endmodule

module atom_msb (
  input  [4:0] opcode,
  input  a,
  input  lost,
  output receive
);

  wire and_1_out, and_2_out;

  and and_1 (and_1_out, ~opcode[4], opcode[3], ~opcode[2], ~opcode[1], opcode[0], a);  // AND_Gate
  and and_2 (and_2_out, ~opcode[4], opcode[3], ~opcode[2], opcode[1], opcode[0], lost);  // AND_Gate
  or or_1 (receive, and_1_out, and_2_out);
endmodule

module atom_slt (
  input  [4:0] opcode,
  input  [31:0] s,
  input  a_msb,
  input  b_msb,
  input  slt,
  output [31:0] r
);

  wire and_5_out, not_1_out;
  wire [0:0] multiplexer_1_out;
  wire [3:0] and_1_out;

  and and_1 (and_1_out[0], a_msb, b_msb);
  and and_2 (and_1_out[1], ~a_msb, ~b_msb);  // AND_Gate
  and and_3 (and_1_out[2], a_msb, ~b_msb);  // AND_Gate
  and and_4 (and_1_out[3], ~a_msb, b_msb);  // AND_Gate
  not not_1 (not_1_out, slt);
  Multiplexer #(.select(4)) multiplexer_1 (
    .in1(not_1_out), .in2(slt), .in4(1'b1), .in8(1'b0), .out(multiplexer_1_out[0]), .sel(and_1_out));  // open: in0, in3, in5, in6, in7, in9, in10, in11, in12, in13, in14, in15, en
  and and_5 (and_5_out, ~opcode[0], ~opcode[1], opcode[2], opcode[3], ~opcode[4]);  // AND_Gate
  Multiplexer #(.width(32)) multiplexer_2 (
    .in0(s), .in1({{31{1'b0}}, multiplexer_1_out[0]}), .out(r), .sel(and_5_out));  // open: en
endmodule
